// Logisim project 8BitCom.circ as structural Verilog: 1 circuit, main circuit main
module main (
  input  OUT,
  input  in_2,
  input  in_3,
  input  in_4,
  input  in_5,
  input  in_6,
  input  in_7,
  input  in_8,
  input  in_9,
  input  in_10,
  input  in_11,
  input  [7:0] in_12,
  input  in_13
);

  wire adder_1_cout, adder_1_out, adder_2_cout, adder_2_out, adder_3_cout, adder_3_out, adder_4_cout,
       adder_4_out, adder_5_cout, adder_5_out, adder_6_cout, adder_6_out, adder_7_cout, adder_7_out,
       adder_8_out, and_1_out, and_2_out, and_3_out, and_4_out, and_5_out, and_6_out, and_7_out, and_8_out,
       and_9_out, and_10_out, and_11_out, and_12_out, and_13_out, and_14_out, and_15_out, and_16_out,
       and_17_out, and_18_out, and_19_out, and_20_out, and_21_out, and_22_out, and_23_out, and_24_out,
       and_25_out, and_26_out, and_27_out, and_28_out, and_29_out, and_30_out, and_31_out, and_32_out,
       and_33_out, clock_1_out, clock_2_out, controlled_buffer_1_out, not_1_out, not_2_out, not_3_out,
       not_4_out, not_5_out, not_6_out, not_7_out, not_8_out, not_9_out, not_10_out, not_11_out, not_12_out,
       not_13_out, not_14_out, not_15_out, not_16_out, not_17_out, not_18_out, not_19_out, not_20_out,
       or_1_out, or_2_out, or_3_out, or_4_out, or_5_out, or_6_out, or_7_out, or_8_out, or_9_out, or_10_out,
       or_11_out, or_12_out, or_13_out, or_14_out, or_15_out, or_16_out, undriven, undriven_2, xor_1_out,
       xor_2_out, xor_3_out, xor_4_out, xor_5_out, xor_6_out, xor_7_out, xor_8_out;
  wire [3:0] controlled_buffer_5_out, counter_1_q, counter_2_q, d_ff_1_q, d_ff_5_q, d_ff_9_q, d_ff_13_q;
  wire [7:0] controlled_buffer_6_out, ram_1_data, register_1_q, register_2_q;
  wire [15:0] rom_1_data;

  assign controlled_buffer_1_out = not_1_out ? clock_1_out : 1'bz;  // Controlled_Buffer controlled_buffer_1
  Clock clock_1 (.out(clock_1_out));
  not not_1 (not_1_out, rom_1_data[15]);
  Button button_1 ();  // open: out
  not not_2 (not_2_out, controlled_buffer_1_out);
  Register register_1 (
    .D(ram_1_data), .en(rom_1_data[9]), .Q(register_1_q), .clk(controlled_buffer_1_out));  // open: clr
  Counter #(.width(4), .max('h8)) counter_1 (.Q(counter_1_q), .clk(and_1_out));  // open: load, D, count, carry, clr
  Clock clock_2 (.out(clock_2_out));
  and and_1 (and_1_out, clock_2_out, not_3_out);
  RAM #(.addrWidth(4), .bus("separate")) ram_1 (
    .addr(controlled_buffer_5_out), .din(ram_1_data), .data(ram_1_data), .str(rom_1_data[11]),
    .sel(rom_1_data[12]), .clk(controlled_buffer_1_out), .ld(rom_1_data[13]), .clr(rom_1_data[10]));
  assign controlled_buffer_5_out[3] = rom_1_data[8] ? register_1_q[3] : 1'bz;  // Controlled_Buffer controlled_buffer_2
  assign controlled_buffer_5_out[2] = rom_1_data[8] ? register_1_q[2] : 1'bz;  // Controlled_Buffer controlled_buffer_3
  not not_3 (not_3_out, rom_1_data[15]);
  assign controlled_buffer_5_out[1] = rom_1_data[8] ? register_1_q[1] : 1'bz;  // Controlled_Buffer controlled_buffer_4
  assign controlled_buffer_5_out[0] = rom_1_data[8] ? register_1_q[0] : 1'bz;  // Controlled_Buffer controlled_buffer_5
  not not_4 (not_4_out, in_13);
  assign controlled_buffer_6_out = not_4_out ? {register_1_q[7:4], counter_1_q} : 8'bz;  // Controlled_Buffer controlled_buffer_6
  assign controlled_buffer_6_out = in_13 ? in_12 : 8'bz;  // Controlled_Buffer controlled_buffer_7
  Counter #(.width(4), .max('hf)) counter_2 (
    .load(rom_1_data[7]), .D(controlled_buffer_5_out), .count(rom_1_data[6]), .Q(counter_2_q),
    .clk(controlled_buffer_1_out));  // open: carry, clr
  ROM #(.dataWidth(16)) rom_1 (.addr(controlled_buffer_6_out), .data(rom_1_data));  // open: sel
  assign controlled_buffer_5_out[3] = rom_1_data[5] ? counter_2_q[3] : 1'bz;  // Controlled_Buffer controlled_buffer_8
  assign controlled_buffer_5_out[2] = rom_1_data[5] ? counter_2_q[2] : 1'bz;  // Controlled_Buffer controlled_buffer_9
  assign controlled_buffer_5_out[1] = rom_1_data[5] ? counter_2_q[1] : 1'bz;  // Controlled_Buffer controlled_buffer_10
  assign controlled_buffer_5_out[0] = rom_1_data[5] ? counter_2_q[0] : 1'bz;  // Controlled_Buffer controlled_buffer_11
  assign ram_1_data[6] = OUT ? in_3 : 1'bz;  // Controlled_Buffer controlled_buffer_12
  assign ram_1_data[7] = OUT ? in_2 : 1'bz;  // Controlled_Buffer controlled_buffer_13
  assign ram_1_data[5] = OUT ? in_4 : 1'bz;  // Controlled_Buffer controlled_buffer_14
  assign ram_1_data[4] = OUT ? in_5 : 1'bz;  // Controlled_Buffer controlled_buffer_15
  assign ram_1_data[3] = OUT ? in_6 : 1'bz;  // Controlled_Buffer controlled_buffer_16
  assign ram_1_data[2] = OUT ? in_7 : 1'bz;  // Controlled_Buffer controlled_buffer_17
  assign ram_1_data[1] = OUT ? in_8 : 1'bz;  // Controlled_Buffer controlled_buffer_18
  not not_5 (not_5_out, rom_1_data[4]);
  and and_2 (and_2_out, not_5_out, d_ff_5_q[3]);
  assign ram_1_data[0] = OUT ? in_9 : 1'bz;  // Controlled_Buffer controlled_buffer_19
  and and_3 (and_3_out, rom_1_data[4], ram_1_data[7]);
  or or_1 (or_1_out, and_2_out, and_3_out);
  not not_6 (not_6_out, rom_1_data[4]);
  and and_4 (and_4_out, not_6_out, d_ff_5_q[2]);
  not not_7 (not_7_out, rom_1_data[4]);
  and and_5 (and_5_out, rom_1_data[4], ram_1_data[6]);
  or or_2 (or_2_out, and_4_out, and_5_out);
  and and_6 (and_6_out, not_7_out, d_ff_5_q[1]);
  and and_7 (and_7_out, rom_1_data[4], ram_1_data[5]);
  or or_3 (or_3_out, and_6_out, and_7_out);
  not not_8 (not_8_out, rom_1_data[4]);
  and and_8 (and_8_out, not_8_out, d_ff_5_q[0]);
  not not_9 (not_9_out, rom_1_data[4]);
  and and_9 (and_9_out, rom_1_data[4], ram_1_data[4]);
  or or_4 (or_4_out, and_8_out, and_9_out);
  and and_10 (and_10_out, rom_1_data[4], ram_1_data[3]);
  and and_11 (and_11_out, not_9_out, d_ff_1_q[3]);
  or or_5 (or_5_out, and_11_out, and_10_out);
  not not_10 (not_10_out, rom_1_data[4]);
  and and_12 (and_12_out, not_10_out, d_ff_1_q[2]);
  not not_11 (not_11_out, rom_1_data[4]);
  and and_13 (and_13_out, rom_1_data[4], ram_1_data[2]);
  or or_6 (or_6_out, and_12_out, and_13_out);
  and and_14 (and_14_out, not_11_out, d_ff_1_q[1]);
  and and_15 (and_15_out, rom_1_data[4], ram_1_data[1]);
  or or_7 (or_7_out, and_14_out, and_15_out);
  not not_12 (not_12_out, rom_1_data[4]);
  and and_16 (and_16_out, not_12_out, d_ff_1_q[0]);
  D_Flip_Flop d_ff_1 (
    .clk(controlled_buffer_1_out), .D(or_8_out), .Q(d_ff_1_q[0]), .en(undriven));  // open: Qn, preset, reset
  D_Flip_Flop d_ff_2 (
    .clk(controlled_buffer_1_out), .D(or_7_out), .Q(d_ff_1_q[1]), .preset(undriven), .en(undriven),
    .reset(undriven));  // open: Qn
  D_Flip_Flop d_ff_3 (
    .clk(controlled_buffer_1_out), .D(or_6_out), .Q(d_ff_1_q[2]), .en(undriven));  // open: Qn, preset, reset
  D_Flip_Flop d_ff_4 (
    .clk(controlled_buffer_1_out), .D(or_5_out), .Q(d_ff_1_q[3]), .en(undriven));  // open: Qn, preset, reset
  D_Flip_Flop d_ff_5 (
    .clk(controlled_buffer_1_out), .D(or_4_out), .Q(d_ff_5_q[0]), .en(undriven));  // open: Qn, preset, reset
  D_Flip_Flop d_ff_6 (
    .clk(controlled_buffer_1_out), .D(or_3_out), .Q(d_ff_5_q[1]), .en(undriven));  // open: Qn, preset, reset
  D_Flip_Flop d_ff_7 (
    .clk(controlled_buffer_1_out), .D(or_2_out), .Q(d_ff_5_q[2]), .en(undriven));  // open: Qn, preset, reset
  D_Flip_Flop d_ff_8 (
    .clk(controlled_buffer_1_out), .D(or_1_out), .Q(d_ff_5_q[3]), .en(undriven));  // open: Qn, preset, reset
  and and_17 (and_17_out, rom_1_data[4], ram_1_data[0]);
  or or_8 (or_8_out, and_16_out, and_17_out);
  LED led_1 (.in(d_ff_1_q[0]));
  LED led_2 (.in(d_ff_1_q[1]));
  LED led_3 (.in(d_ff_1_q[2]));
  LED led_4 (.in(d_ff_1_q[3]));
  LED led_5 (.in(d_ff_5_q[0]));
  LED led_6 (.in(d_ff_5_q[1]));
  LED led_7 (.in(d_ff_5_q[2]));
  LED led_8 (.in(d_ff_5_q[3]));
  not not_13 (not_13_out, rom_1_data[3]);
  and and_18 (and_18_out, not_13_out, d_ff_13_q[3]);
  and and_19 (and_19_out, rom_1_data[3], ram_1_data[7]);
  or or_9 (or_9_out, and_18_out, and_19_out);
  Hex_Digit_Display hex_digit_display_1 (.value(d_ff_5_q));  // open: dp
  Hex_Digit_Display hex_digit_display_2 (.value(d_ff_1_q));  // open: dp
  not not_14 (not_14_out, rom_1_data[3]);
  and and_20 (and_20_out, not_14_out, d_ff_13_q[2]);
  and and_21 (and_21_out, rom_1_data[3], ram_1_data[6]);
  or or_10 (or_10_out, and_20_out, and_21_out);
  not not_15 (not_15_out, rom_1_data[3]);
  and and_22 (and_22_out, rom_1_data[3], ram_1_data[5]);
  and and_23 (and_23_out, not_15_out, d_ff_13_q[1]);
  or or_11 (or_11_out, and_23_out, and_22_out);
  not not_16 (not_16_out, rom_1_data[3]);
  and and_24 (and_24_out, not_16_out, d_ff_13_q[0]);
  Register register_2 (
    .D(ram_1_data), .en(rom_1_data[14]), .Q(register_2_q), .clk(controlled_buffer_1_out));  // open: clr
  and and_25 (and_25_out, rom_1_data[3], ram_1_data[4]);
  or or_12 (or_12_out, and_24_out, and_25_out);
  D_Flip_Flop d_ff_9 (
    .clk(controlled_buffer_1_out), .D(or_16_out), .Q(d_ff_9_q[0]), .en(undriven_2));  // open: Qn, preset, reset
  D_Flip_Flop d_ff_10 (
    .clk(controlled_buffer_1_out), .D(or_15_out), .Q(d_ff_9_q[1]), .en(undriven_2));  // open: Qn, preset, reset
  D_Flip_Flop d_ff_11 (
    .clk(controlled_buffer_1_out), .D(or_14_out), .Q(d_ff_9_q[2]), .en(undriven_2));  // open: Qn, preset, reset
  D_Flip_Flop d_ff_12 (
    .clk(controlled_buffer_1_out), .D(or_13_out), .Q(d_ff_9_q[3]), .en(undriven_2));  // open: Qn, preset, reset
  D_Flip_Flop d_ff_13 (
    .clk(controlled_buffer_1_out), .D(or_12_out), .Q(d_ff_13_q[0]), .en(undriven_2));  // open: Qn, preset, reset
  D_Flip_Flop d_ff_14 (
    .clk(controlled_buffer_1_out), .D(or_11_out), .Q(d_ff_13_q[1]), .en(undriven_2));  // open: Qn, preset, reset
  D_Flip_Flop d_ff_15 (
    .clk(controlled_buffer_1_out), .D(or_10_out), .Q(d_ff_13_q[2]), .en(undriven_2));  // open: Qn, preset, reset
  D_Flip_Flop d_ff_16 (
    .clk(controlled_buffer_1_out), .D(or_9_out), .Q(d_ff_13_q[3]), .en(undriven_2));  // open: Qn, preset, reset
  not not_17 (not_17_out, rom_1_data[3]);
  and and_26 (and_26_out, not_17_out, d_ff_9_q[3]);
  and and_27 (and_27_out, rom_1_data[3], ram_1_data[3]);
  or or_13 (or_13_out, and_26_out, and_27_out);
  LED led_9 (.in(d_ff_9_q[0]));
  LED led_10 (.in(d_ff_9_q[1]));
  LED led_11 (.in(d_ff_9_q[2]));
  LED led_12 (.in(d_ff_9_q[3]));
  LED led_13 (.in(d_ff_13_q[0]));
  LED led_14 (.in(d_ff_13_q[1]));
  LED led_15 (.in(d_ff_13_q[2]));
  LED led_16 (.in(d_ff_13_q[3]));
  not not_18 (not_18_out, rom_1_data[3]);
  and and_28 (and_28_out, not_18_out, d_ff_9_q[2]);
  and and_29 (and_29_out, rom_1_data[3], ram_1_data[2]);
  or or_14 (or_14_out, and_28_out, and_29_out);
  Hex_Digit_Display hex_digit_display_3 (.value(d_ff_9_q));  // open: dp
  Hex_Digit_Display hex_digit_display_4 (.value(d_ff_13_q));  // open: dp
  not not_19 (not_19_out, rom_1_data[3]);
  and and_30 (and_30_out, not_19_out, d_ff_9_q[1]);
  and and_31 (and_31_out, rom_1_data[3], ram_1_data[1]);
  or or_15 (or_15_out, and_30_out, and_31_out);
  Hex_Digit_Display hex_digit_display_5 (.value(register_2_q[7:4]));  // open: dp
  not not_20 (not_20_out, rom_1_data[3]);
  and and_32 (and_32_out, not_20_out, d_ff_9_q[0]);
  Hex_Digit_Display hex_digit_display_6 (.value(register_2_q[3:0]));  // open: dp
  and and_33 (and_33_out, rom_1_data[3], ram_1_data[0]);
  or or_16 (or_16_out, and_32_out, and_33_out);
  Hex_Digit_Display hex_digit_display_7 (.value(ram_1_data[3:0]));  // open: dp
  Hex_Digit_Display hex_digit_display_8 (.value(ram_1_data[7:4]));  // open: dp
  LED led_17 (.in(xor_1_out));
  xor xor_1 (xor_1_out, d_ff_9_q[0], rom_1_data[1]);
  LED led_18 (.in(xor_2_out));
  xor xor_2 (xor_2_out, d_ff_9_q[1], rom_1_data[1]);
  LED led_19 (.in(xor_3_out));
  xor xor_3 (xor_3_out, d_ff_9_q[2], rom_1_data[1]);
  LED led_20 (.in(xor_4_out));
  xor xor_4 (xor_4_out, d_ff_9_q[3], rom_1_data[1]);
  LED led_21 (.in(xor_5_out));
  xor xor_5 (xor_5_out, d_ff_13_q[0], rom_1_data[1]);
  xor xor_6 (xor_6_out, d_ff_13_q[1], rom_1_data[1]);
  LED led_22 (.in(xor_6_out));
  xor xor_7 (xor_7_out, d_ff_13_q[2], rom_1_data[1]);
  LED led_23 (.in(xor_7_out));
  xor xor_8 (xor_8_out, d_ff_13_q[3], rom_1_data[1]);
  LED led_24 (.in(xor_8_out));
  LED led_25 (.in(adder_1_out));
  Adder #(.width(1)) adder_1 (
    .a(d_ff_1_q[0]), .b(xor_1_out), .out(adder_1_out), .cin(rom_1_data[1]), .cout(adder_1_cout));
  Adder #(.width(1)) adder_2 (
    .a(d_ff_1_q[1]), .b(xor_2_out), .out(adder_2_out), .cin(adder_1_cout), .cout(adder_2_cout));
  LED led_26 (.in(adder_2_out));
  Adder #(.width(1)) adder_3 (
    .a(d_ff_1_q[2]), .b(xor_3_out), .out(adder_3_out), .cin(adder_2_cout), .cout(adder_3_cout));
  LED led_27 (.in(adder_3_out));
  LED led_28 (.in(adder_4_out));
  Adder #(.width(1)) adder_4 (
    .a(d_ff_1_q[3]), .b(xor_4_out), .out(adder_4_out), .cin(adder_3_cout), .cout(adder_4_cout));
  LED led_29 (.in(adder_5_out));
  Adder #(.width(1)) adder_5 (
    .a(d_ff_5_q[0]), .b(xor_5_out), .out(adder_5_out), .cin(adder_4_cout), .cout(adder_5_cout));
  LED led_30 (.in(adder_6_out));
  Adder #(.width(1)) adder_6 (
    .a(d_ff_5_q[1]), .b(xor_6_out), .out(adder_6_out), .cin(adder_5_cout), .cout(adder_6_cout));
  LED led_31 (.in(adder_7_out));
  Adder #(.width(1)) adder_7 (
    .a(d_ff_5_q[2]), .b(xor_7_out), .out(adder_7_out), .cin(adder_6_cout), .cout(adder_7_cout));
  LED led_32 (.in(adder_8_out));
  Adder #(.width(1)) adder_8 (.a(d_ff_5_q[3]), .b(xor_8_out), .out(adder_8_out), .cin(adder_7_cout));  // open: cout
  assign ram_1_data[7] = rom_1_data[2] ? adder_8_out : 1'bz;  // Controlled_Buffer controlled_buffer_20
  assign ram_1_data[6] = rom_1_data[2] ? adder_7_out : 1'bz;  // Controlled_Buffer controlled_buffer_21
  assign ram_1_data[4] = rom_1_data[2] ? adder_5_out : 1'bz;  // Controlled_Buffer controlled_buffer_22
  assign ram_1_data[5] = rom_1_data[2] ? adder_6_out : 1'bz;  // Controlled_Buffer controlled_buffer_23
  assign ram_1_data[3] = rom_1_data[2] ? adder_4_out : 1'bz;  // Controlled_Buffer controlled_buffer_24
  assign ram_1_data[2] = rom_1_data[2] ? adder_3_out : 1'bz;  // Controlled_Buffer controlled_buffer_25
  assign ram_1_data[1] = rom_1_data[2] ? adder_2_out : 1'bz;  // Controlled_Buffer controlled_buffer_26
  assign ram_1_data[0] = rom_1_data[2] ? adder_1_out : 1'bz;  // Controlled_Buffer controlled_buffer_27

  // Notes on the sheet:
  //   LOAD
  //   IR
  //   SEL
  //   RAM MODULE
  //   STR
  //   CLR
  //   IRI
  //   IRO
  //   PCI
  //   CNT ENABLED
  //   contents of rom_1 (hex, n*v repeats v):
  //   3220 40 14*0 3220 40 3110 13*0 3220 40 3108 13*0 3220 40 4014 13*0 3220 40 4016 13*0 3220 40 180
  //   13*0 3220 40 14*8000 3220 40 14*0 3220 40 14*0 3220 40 14*0 3220 40 14*0 3220 40 14*0 3220 40 14*0
  //   3220 40 14*0 3220 40 14*0 3220 40
  //   PCO
  //   Program Counter
  //   R1I
  //   R2I
  //   SUB
  //   ALUO
  //   Res IN
  //   LOAD
  //   8 bit register 1
  //   LOAD
  //   8 bit register 2
  //   SUB
  //   ALU
  //   OUT
endmodule
